// Logisim project Lab3_P2_HecDecode.circ as structural Verilog: 2 circuits, main circuit main
module main (
  input  A,
  input  B,
  input  C,
  input  D
);

  wire A_prime_BD_out, A_prime_C_out, AB_prime_C_prime_out, AD_prime_out, B_prime_D_prime_out, BC_out,
       not_1_out, not_2_out, not_3_out, not_4_out, or_1_out, undriven, undriven_2, undriven_3, undriven_4,
       undriven_5, undriven_6;

  not not_1 (not_1_out, A);
  not not_2 (not_2_out, C);
  not not_3 (not_3_out, B);
  not not_4 (not_4_out, D);
  and B_prime_D_prime (B_prime_D_prime_out, not_3_out, not_4_out);
  and A_prime_C (A_prime_C_out, not_1_out, C);
  and BC (BC_out, B, C);
  and AD_prime (AD_prime_out, A, not_4_out);
  and A_prime_BD (A_prime_BD_out, not_1_out, B, D);
  and AB_prime_C_prime (AB_prime_C_prime_out, A, not_3_out, not_2_out);
  or or_1 (or_1_out, B_prime_D_prime_out, A_prime_C_out, BC_out, AD_prime_out, A_prime_BD_out, AB_prime_C_prime_out);
  _7_Segment_Display u_7_segment_display_1 (
    .g(undriven_5), .f(undriven_4), .a(or_1_out), .b(undriven), .e(undriven_6), .d(undriven_3), .c(undriven_2));  // open: dp

  // Notes on the sheet:
  //   A
  //   B
  //   -A
  //   C
  //   -C
  //   -B
  //   D
  //   -D
  //   A
  //   B
  //   C
  //   D
  //   E
  //   F
  //   G
endmodule

module a (
);

  main main_1 ();  // open: A, B, C, D
endmodule
