// Logisim project Lab6_P1_FordThunderbird.circ as structural Verilog: 1 circuit, main circuit main
module main (
  input  L,
  input  R,
  input  H,
  output out_4,
  output out_5,
  output out_6,
  output out_7,
  output out_8,
  output out_9
);

  wire clock_1_out, D1_2_out, D1_q, D2_2_out, D2_q, D2_qn, HQ2_out, I_out, Q1_Q2_2_out, Q1_Q2_L_out,
       Q1_Q2_out, Q1_Q2_R_out, Q1L_out, Q1Q2L_out, Q1Q2R_out, Q1R_out;

  or I (I_out, L, H, R);
  and HQ2 (HQ2_out, D2_q, H);
  or LC (out_4, HQ2_out, Q1Q2L_out);
  and Q1Q2L (Q1Q2L_out, D1_q, D2_q, L);
  and Q1L (Q1L_out, D1_q, L);
  or LB (out_5, HQ2_out, Q1L_out);
  xor Q1_Q2 (Q1_Q2_out, D1_q, D2_q);
  and Q1_Q2_L (Q1_Q2_L_out, L, Q1_Q2_2_out);
  or LA (out_6, HQ2_out, Q1_Q2_L_out);
  Clock clock_1 (.out(clock_1_out));
  D_Flip_Flop D1 (.clk(clock_1_out), .D(D1_2_out), .Q(D1_q));  // open: Qn, preset, en, reset
  and D1_2 (D1_2_out, Q1_Q2_out, I_out);
  D_Flip_Flop D2 (.clk(clock_1_out), .D(D2_2_out), .Q(D2_q), .Qn(D2_qn));  // open: preset, en, reset
  and D2_2 (D2_2_out, I_out, D2_qn);
  or Q1_Q2_2 (Q1_Q2_2_out, D2_q, D1_q);
  and Q1_Q2_R (Q1_Q2_R_out, Q1_Q2_2_out, R);
  or RA (out_7, HQ2_out, Q1_Q2_R_out);
  and Q1R (Q1R_out, D1_q, R);
  or RB (out_8, HQ2_out, Q1R_out);
  or RC (out_9, HQ2_out, Q1Q2R_out);
  and Q1Q2R (Q1Q2R_out, D1_q, D2_q, R);

  // Notes on the sheet:
  //   Q1
  //   Q2
  //   R
  //   L
  //   Q1
  //   Q2
  //   Q1
  //   Q2
  //   R
endmodule
